// Logisim project Осциллограф.circ as structural Verilog: 3 circuits, main circuit main
module main (
);

  wire button_4_out, CHANGE_MOD, clock_1_out, clock_2_out, clock_3_out, clock_4_out, clock_5_out,
       counter_4_carry, DISPLAY_CLR, DISPLAY_UPDATE, MOD_CH, NEXT_PAGE, not_1_out, or_2_out, or_3_out, SAVE,
       SAVE_IRQ, SHOW_IRQ, SHOW_REQUEST, t_ff_2_qn;
  wire [7:0] MEMORY_PAGE, MEMORY_POINTER, multiplexer_2_out, multiplier_2_out, SAVE_PTR, SHOW_PTR;
  wire [15:0] ADC_DATA, counter_2_q, divider_1_out, MEMORY, multiplexer_1_out, multiplier_1_out, ram_1_dout,
       SAVE_BUF, shift_register_1_out, shift_register_1_q0, shift_register_1_q1, shift_register_1_q2,
       shift_register_1_q3, shift_register_1_q4, shift_register_1_q5, shift_register_1_q6,
       shift_register_1_q7, shift_register_1_q8, shift_register_1_q9, shift_register_1_q10,
       shift_register_1_q11, shift_register_1_q12, shift_register_1_q13, shift_register_1_q14,
       shift_register_1_q15, shift_register_1_q16, shift_register_1_q17, shift_register_1_q18,
       shift_register_1_q19, shift_register_1_q20, shift_register_1_q21, shift_register_1_q22,
       shift_register_1_q23, shift_register_1_q24, shift_register_1_q25, shift_register_1_q26,
       shift_register_1_q27, shift_register_1_q28, shift_register_1_q29, shift_register_1_q30,
       shift_register_2_out, shift_register_2_q0, shift_register_2_q1, shift_register_2_q2,
       shift_register_2_q3, shift_register_2_q4, shift_register_2_q5, shift_register_2_q6,
       shift_register_2_q7, shift_register_2_q8, shift_register_2_q9, shift_register_2_q10,
       shift_register_2_q11, shift_register_2_q12, shift_register_2_q13, shift_register_2_q14,
       shift_register_2_q15, shift_register_2_q16, shift_register_2_q17, shift_register_2_q18,
       shift_register_2_q19, shift_register_2_q20, shift_register_2_q21, shift_register_2_q22,
       shift_register_2_q23, shift_register_2_q24, shift_register_2_q25, shift_register_2_q26,
       shift_register_2_q27, shift_register_2_q28, shift_register_2_q29, shift_register_2_q30;

  Hex_Digit_Display hex_digit_display_1 (.value(MEMORY_PAGE[3:0]));  // open: dp
  Button button_1 (.out(NEXT_PAGE));
  Button button_2 (.out(SAVE));
  Button button_3 (.out(SHOW_REQUEST));
  Button button_4 (.out(button_4_out));
  or or_1 (DISPLAY_CLR, button_4_out, CHANGE_MOD);
  Button button_5 (.out(CHANGE_MOD));
  RAM #(.dataWidth(16), .enables("line")) ram_1 (
    .addr(MEMORY_POINTER), .we(SAVE_IRQ), .clk(clock_1_out), .din(SAVE_BUF), .dout(ram_1_dout));
  Clock clock_1 (.out(clock_1_out));
  or or_2 (or_2_out, ~MOD_CH, SHOW_IRQ);  // OR_Gate
  Multiplexer #(.width(16)) multiplexer_1 (.in0(ADC_DATA), .in1(MEMORY), .out(multiplexer_1_out), .sel(MOD_CH));
  Shift_Register #(.length(32), .width(16)) shift_register_1 (
    .shift(or_2_out), .in(multiplexer_1_out), .clk(clock_2_out), .out(shift_register_1_out), .clr(or_3_out),
    .q0(shift_register_1_q0), .q1(shift_register_1_q1), .q2(shift_register_1_q2), .q3(shift_register_1_q3),
    .q4(shift_register_1_q4), .q5(shift_register_1_q5), .q6(shift_register_1_q6), .q7(shift_register_1_q7),
    .q8(shift_register_1_q8), .q9(shift_register_1_q9), .q10(shift_register_1_q10),
    .q11(shift_register_1_q11), .q12(shift_register_1_q12), .q13(shift_register_1_q13),
    .q14(shift_register_1_q14), .q15(shift_register_1_q15), .q16(shift_register_1_q16),
    .q17(shift_register_1_q17), .q18(shift_register_1_q18), .q19(shift_register_1_q19),
    .q20(shift_register_1_q20), .q21(shift_register_1_q21), .q22(shift_register_1_q22),
    .q23(shift_register_1_q23), .q24(shift_register_1_q24), .q25(shift_register_1_q25),
    .q26(shift_register_1_q26), .q27(shift_register_1_q27), .q28(shift_register_1_q28),
    .q29(shift_register_1_q29), .q30(shift_register_1_q30));  // open: load, d0, d1, d2, d3, d4, d5, d6, d7, d8, d9, d10, d11, d12, d13, d14, d15, d16, d17, d18, d19, d20, d21, d22, d23, d24, d25, d26, d27, d28, d29, d30, d31, q31
  Clock clock_2 (.out(clock_2_out));
  or or_3 (or_3_out, DISPLAY_CLR, DISPLAY_UPDATE);
  Shift_Register #(.length(32), .width(16)) shift_register_2 (
    .clk(DISPLAY_UPDATE), .out(shift_register_2_out), .load(DISPLAY_UPDATE), .clr(DISPLAY_CLR),
    .d0(shift_register_1_q0), .q0(shift_register_2_q0), .d1(shift_register_1_q1), .q1(shift_register_2_q1),
    .d2(shift_register_1_q2), .q2(shift_register_2_q2), .d3(shift_register_1_q3), .q3(shift_register_2_q3),
    .d4(shift_register_1_q4), .q4(shift_register_2_q4), .d5(shift_register_1_q5), .q5(shift_register_2_q5),
    .d6(shift_register_1_q6), .q6(shift_register_2_q6), .d7(shift_register_1_q7), .q7(shift_register_2_q7),
    .d8(shift_register_1_q8), .q8(shift_register_2_q8), .d9(shift_register_1_q9), .q9(shift_register_2_q9),
    .d10(shift_register_1_q10), .q10(shift_register_2_q10), .d11(shift_register_1_q11),
    .q11(shift_register_2_q11), .d12(shift_register_1_q12), .q12(shift_register_2_q12),
    .d13(shift_register_1_q13), .q13(shift_register_2_q13), .d14(shift_register_1_q14),
    .q14(shift_register_2_q14), .d15(shift_register_1_q15), .q15(shift_register_2_q15),
    .d16(shift_register_1_q16), .q16(shift_register_2_q16), .d17(shift_register_1_q17),
    .q17(shift_register_2_q17), .d18(shift_register_1_q18), .q18(shift_register_2_q18),
    .d19(shift_register_1_q19), .q19(shift_register_2_q19), .d20(shift_register_1_q20),
    .q20(shift_register_2_q20), .d21(shift_register_1_q21), .q21(shift_register_2_q21),
    .d22(shift_register_1_q22), .q22(shift_register_2_q22), .d23(shift_register_1_q23),
    .q23(shift_register_2_q23), .d24(shift_register_1_q24), .q24(shift_register_2_q24),
    .d25(shift_register_1_q25), .q25(shift_register_2_q25), .d26(shift_register_1_q26),
    .q26(shift_register_2_q26), .d27(shift_register_1_q27), .q27(shift_register_2_q27),
    .d28(shift_register_1_q28), .q28(shift_register_2_q28), .d29(shift_register_1_q29),
    .q29(shift_register_2_q29), .d30(shift_register_1_q30), .q30(shift_register_2_q30),
    .d31(shift_register_1_out));  // open: shift, in, q31
  Shift_Register #(.length(32), .trigger("falling"), .width(16)) shift_register_3 (
    .shift(SAVE_IRQ), .in({16{1'b0}}), .clk(clock_3_out), .out(SAVE_BUF), .load(SAVE),
    .d0(shift_register_2_q0), .d1(shift_register_2_q1), .d2(shift_register_2_q2), .d3(shift_register_2_q3),
    .d4(shift_register_2_q4), .d5(shift_register_2_q5), .d6(shift_register_2_q6), .d7(shift_register_2_q7),
    .d8(shift_register_2_q8), .d9(shift_register_2_q9), .d10(shift_register_2_q10),
    .d11(shift_register_2_q11), .d12(shift_register_2_q12), .d13(shift_register_2_q13),
    .d14(shift_register_2_q14), .d15(shift_register_2_q15), .d16(shift_register_2_q16),
    .d17(shift_register_2_q17), .d18(shift_register_2_q18), .d19(shift_register_2_q19),
    .d20(shift_register_2_q20), .d21(shift_register_2_q21), .d22(shift_register_2_q22),
    .d23(shift_register_2_q23), .d24(shift_register_2_q24), .d25(shift_register_2_q25),
    .d26(shift_register_2_q26), .d27(shift_register_2_q27), .d28(shift_register_2_q28),
    .d29(shift_register_2_q29), .d30(shift_register_2_q30), .d31(shift_register_2_out));  // open: clr, q0, q1, q2, q3, q4, q5, q6, q7, q8, q9, q10, q11, q12, q13, q14, q15, q16, q17, q18, q19, q20, q21, q22, q23, q24, q25, q26, q27, q28, q29, q30, q31
  Clock clock_3 (.out(clock_3_out));
  Counter #(.max('h1f)) counter_1 (
    .Q(SAVE_PTR), .clk(clock_3_out), .clr(not_1_out));  // open: load, D, count, carry, up
  not not_1 (not_1_out, SAVE_IRQ);
  Clock clock_4 (.out(clock_4_out));
  DotMatrix #(.matrixcols(32), .matrixrows(16)) dotmatrix_1 (
    .col0(shift_register_2_q0), .col1(shift_register_2_q1), .col2(shift_register_2_q2),
    .col3(shift_register_2_q3), .col4(shift_register_2_q4), .col5(shift_register_2_q5),
    .col6(shift_register_2_q6), .col7(shift_register_2_q7), .col8(shift_register_2_q8),
    .col9(shift_register_2_q9), .col10(shift_register_2_q10), .col11(shift_register_2_q11),
    .col12(shift_register_2_q12), .col13(shift_register_2_q13), .col14(shift_register_2_q14),
    .col15(shift_register_2_q15), .col16(shift_register_2_q16), .col17(shift_register_2_q17),
    .col18(shift_register_2_q18), .col19(shift_register_2_q19), .col20(shift_register_2_q20),
    .col21(shift_register_2_q21), .col22(shift_register_2_q22), .col23(shift_register_2_q23),
    .col24(shift_register_2_q24), .col25(shift_register_2_q25), .col26(shift_register_2_q26),
    .col27(shift_register_2_q27), .col28(shift_register_2_q28), .col29(shift_register_2_q29),
    .col30(shift_register_2_q30), .col31(shift_register_2_out));
  Counter #(.max('h1a), .width(16)) counter_2 (
    .Q(counter_2_q), .clk(clock_4_out));  // open: load, D, count, carry, up, clr
  // Probe on MEMORY
  assign MEMORY = SHOW_IRQ ? ram_1_dout : 16'bz;  // Controlled_Buffer controlled_buffer_1
  Multiplier #(.width(16)) multiplier_1 (.a(16'h1000), .b(counter_2_q), .out(multiplier_1_out));  // open: cin, cout
  Divider #(.width(16)) divider_1 (.a(multiplier_1_out), .b(16'h1000), .out(divider_1_out));  // open: upper, rem
  Comparator #(.mode("unsigned"), .width(16)) comparator_1 (
    .a({16{1'b0}}), .b(shift_register_1_out), .lt(DISPLAY_UPDATE));  // open: gt, eq
  Comparator #(.mode("unsigned"), .width(16)) comparator_2 (
    .a(SAVE_BUF), .b({16{1'b0}}), .gt(SAVE_IRQ));  // open: eq, lt
  T_Flip_Flop t_ff_1 (.T(1'b1), .clk(CHANGE_MOD), .Q(MOD_CH));  // open: Qn, reset, preset
  Shifter #(.width(16)) shifter_1 (.in(16'h1), .\dist (divider_1_out[3:0]), .out(ADC_DATA));
  // Probe on multiplexer_2_out
  Multiplexer #(.width(8)) multiplexer_2 (.in0(SAVE_PTR), .in1(SHOW_PTR), .out(multiplexer_2_out), .sel(MOD_CH));
  Counter #(.max('h7)) counter_3 (.Q(MEMORY_PAGE), .clk(NEXT_PAGE));  // open: load, D, count, carry, up, clr
  Clock clock_5 (.out(clock_5_out));
  T_Flip_Flop t_ff_2 (.T(t_ff_2_qn), .clk(SHOW_REQUEST), .Qn(t_ff_2_qn), .reset(counter_4_carry));  // open: Q, preset
  // Probe on multiplier_2_out
  Multiplier multiplier_2 (.a(8'h20), .b(MEMORY_PAGE), .out(multiplier_2_out));  // open: cin, cout
  Counter #(.max('h20)) counter_4 (
    .carry(counter_4_carry), .clk(clock_5_out), .clr(t_ff_2_qn));  // open: load, D, count, Q, up
  Counter #(.max('h1f)) counter_5 (
    .Q(SHOW_PTR), .clk(clock_5_out), .clr(t_ff_2_qn));  // open: load, D, count, carry, up
  // Probe on MEMORY_POINTER
  Adder adder_1 (.a(multiplexer_2_out), .b(multiplier_2_out), .out(MEMORY_POINTER));  // open: cin, cout
  not not_2 (SHOW_IRQ, t_ff_2_qn);

  // Notes on the sheet:
  //   Memory
  //   Signal generator
  //   Accumulate register
  //   Present register
  //   Save register
  //   input value
  //   bit step
  //   ADC
  //   Addr in page
  //   RAM Page shift
  //   Show mode ticker
endmodule

module bitwise_y_and_pixel (
  input  [15:0] input_value,
  input  [15:0] in_2,
  output [15:0] out_3
);

  wire [15:0] divider_1_out, divider_2_out, shifter_2_out;

  Divider #(.width(16)) divider_1 (.a(input_value), .b(in_2), .out(divider_1_out));  // open: upper, rem
  Shifter #(.width(16)) shifter_1 (.in(16'h1), .\dist (divider_1_out[3:0]), .out(out_3));
  Divider #(.width(16)) divider_2 (.a(16'h7d00), .b(16'h1000), .out(divider_2_out));  // open: upper, rem
  Shifter #(.width(16)) shifter_2 (.in(16'h1), .\dist (divider_2_out[3:0]), .out(shifter_2_out));

  // Notes on the sheet:
  //   bit step
  //   input value
  //   bit step
endmodule

module IRQ_QUERY (
  input  in_1,
  input  in_2,
  input  in_3,
  input  in_4,
  input  in_5,
  input  in_6,
  input  in_7,
  input  in_8,
  input  in_9,
  output out_10,
  output out_11,
  output out_12,
  output out_13,
  output [1:0] out_14,
  output out_15
);

  wire t_ff_1_qn, t_ff_2_qn, t_ff_3_qn, t_ff_4_qn;

  T_Flip_Flop t_ff_1 (.T(t_ff_1_qn), .clk(in_1), .Q(out_10), .Qn(t_ff_1_qn), .reset(in_5));  // open: preset
  buf buffer_1 (in_5, in_9);
  T_Flip_Flop t_ff_2 (.T(t_ff_2_qn), .clk(in_2), .Q(out_11), .Qn(t_ff_2_qn), .reset(in_6));  // open: preset
  buf buffer_2 (in_6, in_9);
  T_Flip_Flop t_ff_3 (.T(t_ff_3_qn), .clk(in_3), .Q(out_12), .Qn(t_ff_3_qn), .reset(in_7));  // open: preset
  buf buffer_3 (in_7, in_9);
  T_Flip_Flop t_ff_4 (.T(t_ff_4_qn), .clk(in_4), .Q(out_13), .Qn(t_ff_4_qn), .reset(in_8));  // open: preset
  buf buffer_4 (in_8, in_9);
  Priority_Encoder #(.select(2)) priority_encoder_1 (
    .in0(out_10), .in1(out_11), .in2(out_12), .in3(out_13), .out(out_14), .gs(out_15));  // open: en_out, en_in
endmodule
